// Logisim project 2base32digitCalc.circ as structural Verilog: 3 circuits, main circuit main
module add1 (
  input  in_1,
  input  in_2,
  input  [7:0] in_3,
  input  [7:0] in_4,
  output [7:0] out_5,
  output out_6
);

  wire main_1_t_1, main_2_t_1, main_3_t_1, main_4_t_1, main_5_t_1, main_6_t_1, main_7_t_1;

  main main_1 (.in_1(in_1), .x(in_2), .in_3(in_3[0]), .y(in_4[0]), .out_5(out_5[0]), .t_1(main_1_t_1));
  main main_2 (.in_1(in_1), .x(main_1_t_1), .in_3(in_3[1]), .y(in_4[1]), .out_5(out_5[1]), .t_1(main_2_t_1));
  main main_3 (.in_1(in_1), .x(main_2_t_1), .in_3(in_3[2]), .y(in_4[2]), .out_5(out_5[2]), .t_1(main_3_t_1));
  main main_4 (.in_1(in_1), .x(main_3_t_1), .in_3(in_3[3]), .y(in_4[3]), .out_5(out_5[3]), .t_1(main_4_t_1));
  main main_5 (.in_1(in_1), .x(main_4_t_1), .in_3(in_3[4]), .y(in_4[4]), .out_5(out_5[4]), .t_1(main_5_t_1));
  main main_6 (.in_1(in_1), .x(main_5_t_1), .in_3(in_3[5]), .y(in_4[5]), .out_5(out_5[5]), .t_1(main_6_t_1));
  main main_7 (.in_1(in_1), .x(main_6_t_1), .in_3(in_3[6]), .y(in_4[6]), .out_5(out_5[6]), .t_1(main_7_t_1));
  main main_8 (.in_1(in_1), .x(main_7_t_1), .in_3(in_3[7]), .y(in_4[7]), .out_5(out_5[7]), .t_1(out_6));
endmodule

module main (
  input  in_1,
  input  x,
  input  in_3,
  input  y,
  output out_5,
  output t_1
);

  wire and_1_out, and_2_out, and_3_out, and_4_out, and_5_out, and_6_out, not_1_out, not_2_out, not_3_out,
       not_4_out, not_5_out, q_out, xor_1_out, xor_2_out;

  not not_1 (not_1_out, in_1);
  not not_2 (not_2_out, y);
  not not_3 (not_3_out, in_3);
  xor xor_1 (xor_1_out, in_3, not_1_out);
  and and_1 (and_1_out, in_3, not_2_out);
  and and_2 (and_2_out, not_3_out, y);
  and and_3 (and_3_out, xor_1_out, y);
  or q (q_out, and_1_out, and_2_out);
  not not_4 (not_4_out, q_out);
  not not_5 (not_5_out, x);
  xor xor_2 (xor_2_out, q_out, not_1_out);
  and and_4 (and_4_out, x, not_4_out);
  and and_5 (and_5_out, q_out, not_5_out);
  and and_6 (and_6_out, x, xor_2_out);
  or d (out_5, and_4_out, and_5_out);
  or or_1 (t_1, and_6_out, and_3_out);

  // Notes on the sheet:
  //   s/a
endmodule

module add2 (
  input  in_1,
  input  in_2,
  input  [31:0] in_3,
  input  [31:0] in_4,
  output [31:0] out_5,
  output out_6
);

  wire add1_1_out_6, add1_2_out_6, add1_3_out_6;

  add1 add1_1 (.in_1(in_1), .in_2(in_2), .in_3(in_3[7:0]), .in_4(in_4[7:0]), .out_5(out_5[7:0]), .out_6(add1_1_out_6));
  add1 add1_2 (
    .in_1(in_1), .in_2(add1_1_out_6), .in_3(in_3[15:8]), .in_4(in_4[15:8]), .out_5(out_5[15:8]),
    .out_6(add1_2_out_6));
  add1 add1_3 (
    .in_1(in_1), .in_2(add1_2_out_6), .in_3(in_3[23:16]), .in_4(in_4[23:16]), .out_5(out_5[23:16]),
    .out_6(add1_3_out_6));
  add1 add1_4 (
    .in_1(in_1), .in_2(add1_3_out_6), .in_3(in_3[31:24]), .in_4(in_4[31:24]), .out_5(out_5[31:24]),
    .out_6(out_6));
endmodule
