// Logisim project 2base4digitAdder.circ as structural Verilog: 1 circuit, main circuit main
module main (
  input  ki,
  input  [7:0] in_2,
  input  [7:0] in_3,
  output [7:0] out_4
);

  wire and_1_out, and_2_out, and_3_out, and_4_out, and_5_out, and_6_out, and_7_out, and_8_out, and_9_out,
       and_10_out, and_11_out, and_12_out, and_13_out, and_14_out, and_15_out, and_16_out, and_17_out,
       and_18_out, and_19_out, and_20_out, and_21_out, and_22_out, and_23_out, and_24_out, not_1_out,
       not_2_out, not_3_out, not_4_out, not_5_out, not_6_out, not_7_out, not_8_out, not_9_out, not_10_out,
       not_11_out, not_12_out, not_13_out, not_14_out, not_15_out, not_16_out, or_1_out, or_2_out, or_3_out,
       qi_2_out, qi_3_out, qi_4_out, qi_out;

  not not_1 (not_1_out, in_3[0]);
  not not_2 (not_2_out, in_2[0]);
  not not_3 (not_3_out, in_3[2]);
  not not_4 (not_4_out, in_2[2]);
  and and_1 (and_1_out, in_2[0], not_1_out);
  and and_2 (and_2_out, not_2_out, in_3[0]);
  and and_3 (and_3_out, in_2[2], not_3_out);
  and and_4 (and_4_out, not_4_out, in_3[2]);
  or qi (qi_out, and_1_out, and_2_out);
  or qi_2 (qi_2_out, and_3_out, and_4_out);
  and and_5 (and_5_out, in_2[0], in_3[0]);
  and and_6 (and_6_out, qi_out, ki);
  not not_5 (not_5_out, qi_out);
  and and_7 (and_7_out, not_5_out, ki);
  and and_8 (and_8_out, qi_out, not_6_out);
  not not_6 (not_6_out, ki);
  and and_9 (and_9_out, in_2[2], in_3[2]);
  and and_10 (and_10_out, qi_2_out, or_3_out);
  not not_7 (not_7_out, qi_2_out);
  not not_8 (not_8_out, or_3_out);
  or or_1 (or_1_out, and_5_out, and_6_out);
  or si (out_4[0], and_7_out, and_8_out);
  or or_2 (or_2_out, and_9_out, and_10_out);
  and and_11 (and_11_out, not_7_out, or_3_out);
  and and_12 (and_12_out, qi_2_out, not_8_out);
  not not_9 (not_9_out, in_3[1]);
  not not_10 (not_10_out, in_2[1]);
  or si_2 (out_4[2], and_11_out, and_12_out);
  and and_13 (and_13_out, in_2[1], not_9_out);
  and and_14 (and_14_out, not_10_out, in_3[1]);
  or qi_3 (qi_3_out, and_13_out, and_14_out);
  and and_15 (and_15_out, in_2[1], in_3[1]);
  and and_16 (and_16_out, qi_3_out, or_1_out);
  not not_11 (not_11_out, qi_3_out);
  not not_12 (not_12_out, or_1_out);
  not not_13 (not_13_out, in_3[3]);
  not not_14 (not_14_out, in_2[3]);
  or or_3 (or_3_out, and_15_out, and_16_out);
  and and_17 (and_17_out, not_11_out, or_1_out);
  and and_18 (and_18_out, qi_3_out, not_12_out);
  and and_19 (and_19_out, in_2[3], not_13_out);
  and and_20 (and_20_out, not_14_out, in_3[3]);
  or si_3 (out_4[1], and_17_out, and_18_out);
  or qi_4 (qi_4_out, and_19_out, and_20_out);
  and and_21 (and_21_out, in_2[3], in_3[3]);
  and and_22 (and_22_out, qi_4_out, or_2_out);
  not not_15 (not_15_out, qi_4_out);
  and and_23 (and_23_out, not_15_out, or_2_out);
  and and_24 (and_24_out, qi_4_out, not_16_out);
  not not_16 (not_16_out, or_2_out);
  or or_4 (out_4[4], and_21_out, and_22_out);
  or si_4 (out_4[3], and_23_out, and_24_out);

  // Notes on the sheet:
  //   x1
  //   y1
  //   x1
  //   y1
  //   ki
  //   x1
  //   y1
  //   ki+1
  //   ki
  //   ki+1
  //   x1
  //   y1
  //   ki
  //   ki+1
  //   ki+1
endmodule
