// Logisim project comparer.circ as structural Verilog: 4 circuits, main circuit main
module add1 (
  input  in_1,
  input  in_2,
  input  [7:0] in_3,
  input  [7:0] y,
  output [7:0] out_5,
  output out_6,
  output x_y,
  output y_x
);

  wire main_1_t_1, main_2_t_1, main_3_t_1, main_4_t_1, main_5_t_1, main_6_t_1, main_7_t_1;

  x_y x_y_1 (.x(in_3[7]), .y(y[7]), .d(out_5[7]), .out_4(x_y));
  x_y x_y_2 (.x(y[7]), .y(in_3[7]), .d(out_5[7]), .out_4(y_x));
  main main_1 (.in_1(in_1), .x(in_2), .in_3(in_3[0]), .y(y[0]), .out_5(out_5[0]), .t_1(main_1_t_1));
  main main_2 (.in_1(in_1), .x(main_1_t_1), .in_3(in_3[1]), .y(y[1]), .out_5(out_5[1]), .t_1(main_2_t_1));
  main main_3 (.in_1(in_1), .x(main_2_t_1), .in_3(in_3[2]), .y(y[2]), .out_5(out_5[2]), .t_1(main_3_t_1));
  main main_4 (.in_1(in_1), .x(main_3_t_1), .in_3(in_3[3]), .y(y[3]), .out_5(out_5[3]), .t_1(main_4_t_1));
  main main_5 (.in_1(in_1), .x(main_4_t_1), .in_3(in_3[4]), .y(y[4]), .out_5(out_5[4]), .t_1(main_5_t_1));
  main main_6 (.in_1(in_1), .x(main_5_t_1), .in_3(in_3[5]), .y(y[5]), .out_5(out_5[5]), .t_1(main_6_t_1));
  main main_7 (.in_1(in_1), .x(main_6_t_1), .in_3(in_3[6]), .y(y[6]), .out_5(out_5[6]), .t_1(main_7_t_1));
  main main_8 (.in_1(in_1), .x(main_7_t_1), .in_3(in_3[7]), .y(y[7]), .out_5(out_5[7]), .t_1(out_6));

  // Notes on the sheet:
  //   x
endmodule

module main (
  input  in_1,
  input  x,
  input  in_3,
  input  y,
  output out_5,
  output t_1
);

  wire and_1_out, and_2_out, and_3_out, and_4_out, and_5_out, and_6_out, not_1_out, not_2_out, not_3_out,
       not_4_out, not_5_out, q_out, xor_1_out, xor_2_out;

  not not_1 (not_1_out, in_1);
  not not_2 (not_2_out, y);
  not not_3 (not_3_out, in_3);
  xor xor_1 (xor_1_out, in_3, not_1_out);
  and and_1 (and_1_out, in_3, not_2_out);
  and and_2 (and_2_out, not_3_out, y);
  and and_3 (and_3_out, xor_1_out, y);
  or q (q_out, and_1_out, and_2_out);
  not not_4 (not_4_out, q_out);
  not not_5 (not_5_out, x);
  xor xor_2 (xor_2_out, q_out, not_1_out);
  and and_4 (and_4_out, x, not_4_out);
  and and_5 (and_5_out, q_out, not_5_out);
  and and_6 (and_6_out, x, xor_2_out);
  or d (out_5, and_4_out, and_5_out);
  or or_1 (t_1, and_6_out, and_3_out);

  // Notes on the sheet:
  //   s/a
endmodule

module comparator (
  input  s_a,
  input  t0,
  input  x,
  input  y,
  output L,
  output t_i_1
);

  wire and_1_out, and_2_out, and_3_out, and_4_out, main_1_out_5, not_1_out, not_2_out, not_3_out, or_1_out;

  not not_1 (not_1_out, x);
  main main_1 (.in_1(s_a), .x(t0), .in_3(x), .y(y), .out_5(main_1_out_5), .t_1(t_i_1));
  not not_2 (not_2_out, y);
  and and_1 (and_1_out, not_1_out, y);
  and and_2 (and_2_out, x, not_2_out);
  and and_3 (and_3_out, and_1_out, main_1_out_5);
  not not_3 (not_3_out, main_1_out_5);
  and and_4 (and_4_out, not_3_out, and_2_out);
  or or_1 (or_1_out, and_3_out, and_4_out);
  xor xor_1 (L, main_1_out_5, or_1_out);

  // Notes on the sheet:
  //   d
  //   o
  //   L = x < y ? 1 : 0
endmodule

module x_y (
  input  x,
  input  y,
  input  d,
  output out_4
);

  wire and_1_out, and_2_out, and_3_out, and_4_out, not_1_out, not_2_out, not_3_out, O_out;

  not not_1 (not_1_out, x);
  not not_2 (not_2_out, y);
  and and_1 (and_1_out, not_1_out, y);
  not not_3 (not_3_out, d);
  and and_2 (and_2_out, not_2_out, x);
  and and_3 (and_3_out, and_1_out, d);
  and and_4 (and_4_out, not_3_out, and_2_out);
  or O (O_out, and_3_out, and_4_out);
  xor L (out_4, d, O_out);

  // Notes on the sheet:
  //   L = x < y ? 1 : 0
endmodule
