// Logisim project nand2.circ as structural Verilog: 1 circuit, main circuit main
module main (
  input  [7:0] in_1,
  output [7:0] out_2
);

  wire transistor_3_out;

  Transistor transistor_1 (.in(1'b1), .out(out_2[0]), .gate(in_1[1]));
  Transistor #(.\type ("n")) transistor_2 (.in(transistor_3_out), .out(out_2[0]), .gate(in_1[1]));
  Transistor #(.\type ("n"), .gate("br")) transistor_3 (.in(1'b0), .out(transistor_3_out), .gate(in_1[0]));
  Transistor #(.gate("br")) transistor_4 (.in(1'b1), .out(out_2[0]), .gate(in_1[0]));
endmodule
