// Logisim project nand2Macro.circ as structural Verilog: 3 circuits, main circuit nand2
module nand2 (
  input  [7:0] in_1,
  output [7:0] out_2
);

  wire transistor_3_out;

  Transistor transistor_1 (.in(1'b1), .out(out_2[0]), .gate(in_1[1]));
  Transistor #(.\type ("n")) transistor_2 (.in(transistor_3_out), .out(out_2[0]), .gate(in_1[1]));
  Transistor #(.\type ("n"), .gate("br")) transistor_3 (.in(1'b0), .out(transistor_3_out), .gate(in_1[0]));
  Transistor #(.gate("br")) transistor_4 (.in(1'b1), .out(out_2[0]), .gate(in_1[0]));
endmodule

module Gate1 (
  input  in_1,
  output out_2
);

  wire [7:1] nand2_1_out_2;
  wire [7:2] undriven;

  nand2 nand2_1 (.in_1({undriven, {2{in_1}}}), .out_2({nand2_1_out_2, out_2}));
endmodule

module Gate2 (
  input  in_1,
  input  in_2,
  output out_3
);

  wire [7:0] nand2_1_out_2;
  wire [7:1] nand2_2_out_2;
  wire [7:2] undriven, undriven_2;

  nand2 nand2_1 (.in_1({undriven, in_2, in_1}), .out_2(nand2_1_out_2));
  nand2 nand2_2 (.in_1({undriven_2, {2{nand2_1_out_2[0]}}}), .out_2({nand2_2_out_2, out_3}));
endmodule
