// Logisim project nand_and_not_or_nor.circ as structural Verilog: 1 circuit, main circuit main
module main (
  input  NOT,
  input  AND,
  input  in_3,
  input  NAND,
  input  in_5,
  input  in_6,
  input  in_7,
  input  in_8,
  input  in_9,
  output out_10,
  output out_11,
  output out_12,
  output out_13,
  output out_14
);

  wire transistor_1_out, transistor_3_out, transistor_4_out, transistor_6_out, transistor_7_out,
       transistor_9_out, transistor_10_out, transistor_12_out, transistor_19_out, transistor_23_out,
       transistor_25_out, transistor_28_out, transistor_29_out, transistor_32_out, transistor_36_out,
       transistor_40_out, transistor_41_out, transistor_44_out, transistor_48_out;

  Transistor transistor_1 (.in(1'b1), .out(transistor_1_out), .gate(in_6));
  Transistor #(.\type ("n")) transistor_2 (.in(transistor_3_out), .out(transistor_1_out), .gate(in_6));
  Transistor #(.\type ("n"), .gate("br")) transistor_3 (.in(1'b0), .out(transistor_3_out), .gate(in_6));
  Transistor transistor_4 (.in(1'b1), .out(transistor_4_out), .gate(in_8));
  Transistor #(.\type ("n")) transistor_5 (.in(transistor_6_out), .out(transistor_4_out), .gate(in_8));
  Transistor #(.\type ("n"), .gate("br")) transistor_6 (.in(1'b0), .out(transistor_6_out), .gate(in_8));
  Transistor transistor_7 (.in(1'b1), .out(transistor_7_out), .gate(in_3));
  Transistor #(.\type ("n")) transistor_8 (.in(transistor_9_out), .out(transistor_7_out), .gate(in_3));
  Transistor #(.\type ("n"), .gate("br")) transistor_9 (.in(1'b0), .out(transistor_9_out), .gate(AND));
  Transistor transistor_10 (.in(1'b1), .out(transistor_10_out), .gate(AND));
  Transistor #(.\type ("n")) transistor_11 (.in(transistor_12_out), .out(transistor_10_out), .gate(AND));
  Transistor #(.\type ("n"), .gate("br")) transistor_12 (.in(1'b0), .out(transistor_12_out), .gate(in_3));
  Transistor #(.gate("br")) transistor_13 (.in(1'b1), .out(transistor_1_out), .gate(in_6));
  Transistor #(.gate("br")) transistor_14 (.in(1'b1), .out(transistor_4_out), .gate(in_8));
  Transistor #(.gate("br")) transistor_15 (.in(1'b1), .out(transistor_7_out), .gate(AND));
  Transistor #(.gate("br")) transistor_16 (.in(1'b1), .out(transistor_10_out), .gate(in_3));
  Transistor transistor_17 (.in(1'b1), .out(out_13), .gate(transistor_4_out));
  Transistor #(.\type ("n")) transistor_18 (.in(transistor_19_out), .out(out_13), .gate(transistor_4_out));
  Transistor #(.\type ("n"), .gate("br")) transistor_19 (.in(1'b0), .out(transistor_19_out), .gate(transistor_1_out));
  Transistor transistor_20 (.in(1'b1), .out(out_11), .gate(transistor_10_out));
  Transistor #(.gate("br")) transistor_21 (.in(1'b1), .out(out_11), .gate(transistor_7_out));
  Transistor #(.\type ("n")) transistor_22 (.in(transistor_23_out), .out(out_11), .gate(transistor_10_out));
  Transistor #(.\type ("n"), .gate("br")) transistor_23 (.in(1'b0), .out(transistor_23_out), .gate(transistor_7_out));
  Transistor #(.gate("br")) transistor_24 (.in(1'b1), .out(out_13), .gate(transistor_1_out));
  Transistor #(.gate("br")) transistor_25 (.in(1'b1), .out(transistor_25_out), .gate(in_7));
  Transistor transistor_26 (.in(1'b1), .out(transistor_25_out), .gate(in_7));
  Transistor #(.\type ("n")) transistor_27 (.in(transistor_28_out), .out(transistor_25_out), .gate(in_7));
  Transistor #(.\type ("n"), .gate("br")) transistor_28 (.in(1'b0), .out(transistor_28_out), .gate(in_7));
  Transistor #(.gate("br")) transistor_29 (.in(1'b1), .out(transistor_29_out), .gate(in_9));
  Transistor transistor_30 (.in(1'b1), .out(transistor_29_out), .gate(in_9));
  Transistor #(.\type ("n")) transistor_31 (.in(transistor_32_out), .out(transistor_29_out), .gate(in_9));
  Transistor #(.\type ("n"), .gate("br")) transistor_32 (.in(1'b0), .out(transistor_32_out), .gate(in_9));
  Transistor transistor_33 (.in(1'b1), .out(out_10), .gate(NOT));
  Transistor #(.gate("br")) transistor_34 (.in(1'b1), .out(out_10), .gate(NOT));
  Transistor #(.\type ("n")) transistor_35 (.in(transistor_36_out), .out(out_10), .gate(NOT));
  Transistor #(.\type ("n"), .gate("br")) transistor_36 (.in(1'b0), .out(transistor_36_out), .gate(NOT));
  Transistor transistor_37 (.in(1'b1), .out(out_12), .gate(in_5));
  Transistor #(.gate("br")) transistor_38 (.in(1'b1), .out(out_12), .gate(NAND));
  Transistor #(.\type ("n")) transistor_39 (.in(transistor_40_out), .out(out_12), .gate(in_5));
  Transistor #(.\type ("n"), .gate("br")) transistor_40 (.in(1'b0), .out(transistor_40_out), .gate(NAND));
  Transistor transistor_41 (.in(1'b1), .out(transistor_41_out), .gate(transistor_29_out));
  Transistor #(.gate("br")) transistor_42 (.in(1'b1), .out(transistor_41_out), .gate(transistor_25_out));
  Transistor #(.\type ("n")) transistor_43 (.in(transistor_44_out), .out(transistor_41_out), .gate(transistor_29_out));
  Transistor #(.\type ("n"), .gate("br")) transistor_44 (.in(1'b0), .out(transistor_44_out), .gate(transistor_25_out));
  Transistor transistor_45 (.in(1'b1), .out(out_14), .gate(transistor_41_out));
  Transistor #(.gate("br")) transistor_46 (.in(1'b1), .out(out_14), .gate(transistor_41_out));
  Transistor #(.\type ("n")) transistor_47 (.in(transistor_48_out), .out(out_14), .gate(transistor_41_out));
  Transistor #(.\type ("n"), .gate("br")) transistor_48 (.in(1'b0), .out(transistor_48_out), .gate(transistor_41_out));

  // Notes on the sheet:
  //   OR
  //   NOR
endmodule
