// Logisim project ram.circ as structural Verilog: 1 circuit, main circuit main
module main (
  input  [7:0] in_1,
  input  [2:0] in_2,
  input  in_3,
  input  [2:0] in_4,
  input  in_5,
  input  in_6,
  input  in_7,
  input  in_8,
  input  [7:0] in_9,
  input  in_10,
  input  en,
  input  in_12,
  input  [3:0] in_13,
  input  clr,
  input  in_15,
  output [7:0] out_16,
  output out_17,
  output out_18,
  output [7:0] out_19
);

  wire clock_1_out, multiplexer_1_out, multiplexer_2_out, not_1_out;
  wire [3:0] adder_1_out, register_1_q;
  wire [7:0] adder_2_out, register_2_q;

  Multiplexer multiplexer_1 (.in0(in_5), .in1(in_6), .out(multiplexer_1_out), .sel(in_10), .en(in_8));
  Demultiplexer demultiplexer_1 (.out0(out_17), .out1(out_18), .in(multiplexer_1_out), .sel(in_10), .en(in_8));
  Demultiplexer #(.select(3)) demultiplexer_2 (
    .out0(out_16[0]), .out1(out_16[1]), .out2(out_16[2]), .out3(out_16[3]), .out4(out_16[4]),
    .out5(out_16[5]), .out6(out_16[6]), .out7(out_16[7]), .in(multiplexer_2_out), .sel(in_4), .en(in_3));
  Multiplexer #(.select(3)) multiplexer_2 (
    .in0(in_1[0]), .in1(in_1[1]), .in2(in_1[2]), .in3(in_1[3]), .in4(in_1[4]), .in5(in_1[5]), .in6(in_1[6]),
    .in7(in_1[7]), .out(multiplexer_2_out), .sel(in_2), .en(in_3));
  Register #(.width(4)) register_1 (.D(adder_1_out), .en(en), .Q(register_1_q), .clk(clock_1_out), .clr(clr));
  Adder #(.width(4)) adder_1 (.a(in_13), .b(register_1_q), .out(adder_1_out), .cin(in_12));  // open: cout
  Clock clock_1 (.out(clock_1_out));
  RAM #(.addrWidth(4)) ram_1 (.addr(register_1_q), .data(out_19), .sel(en), .clk(clock_1_out), .ld(in_15), .clr(clr));
  Register register_2 (.D(adder_2_out), .en(en), .Q(register_2_q), .clk(clock_1_out), .clr(clr));
  not not_1 (not_1_out, in_15);
  Adder adder_2 (.a(in_9), .b(register_2_q), .out(adder_2_out), .cin(in_7));  // open: cout
  assign out_19 = not_1_out ? register_2_q : 8'bz;  // Controlled_Buffer controlled_buffer_1

  // Notes on the sheet:
  //   1 READ
  //   ld
  //   0 WRITE
  //   clk
endmodule
